# Fritzing sketch psoc_3sensor_connection (saved by Fritzing 1.0.5)
breadboards: 1

parts:
  TLE493D-P3xx-MS2GO1 = TLE493D-P3xx-MS2GO [part_number=TLE493DP3XXMS2GOTOBO1]
  A1 = CY8CKIT-062S2-AI [part_number=CY8CKIT-062S2-AI]
  TLE493D-P3xx-MS2GO2 = TLE493D-P3xx-MS2GO [part_number=TLE493DP3XXMS2GOTOBO1]
  TLE493D-P3xx-MS2GO3 = TLE493D-P3xx-MS2GO [part_number=TLE493DP3XXMS2GOTOBO1]

nets:
  N1: TLE493D-P3xx-MS2GO1.VDD2, A1.P9_7
  N2: TLE493D-P3xx-MS2GO1.MOSI, A1.P9_0
  N3: TLE493D-P3xx-MS2GO1.MISO, A1.P9_1
  N4: TLE493D-P3xx-MS2GO1.NCS, A1.P9_3
  N5: TLE493D-P3xx-MS2GO1.SCK, A1.P9_2
  GND: TLE493D-P3xx-MS2GO1.GND, A1.GND
  N6: A1.P9_4, TLE493D-P3xx-MS2GO2.NCS
  N7: A1.P9_5, TLE493D-P3xx-MS2GO3.NCS

notes:
  Careful with CLK and CS on sensor!!!
  yellow: MOSI
  green: MISO
  black: CLK
  Other 3 line: CS
  Skip SPI, as above

custom parts:
  TLE493D-P3xx-MS2GO: The kit features two 3D Hall sensors for magnetic measurement from the 3rd Generation, with I²C and SPI interfaces. It includes an ARM Cortex-M0 CPU and an on-board debugger. A dedicated GUI enables fast and easy plug-and-play system development.
  CY8CKIT-062S2-AI: The PSoC™ 6 AI Evaluation Kit is a Hardware platform focused on Machine Learning (ML) . It enables customers to evaluate Infineon’s ML platform Imagimob Studio, as well as ready to deploy ML models, and other software products. Data collection is enabled via PSoC™ 6 MCU, radar, acoustic, pressure & IMU sensors. The board is designed for easy prototyping and lets customers collect real-life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
